// Logisim project 第13組 Hexidecimal to 7S-LED decoder.circ as structural Verilog: 1 circuit, main circuit main
module main (
  input  D,
  input  C,
  input  B,
  input  A,
  output out_5,
  output out_6,
  output out_7,
  output out_8,
  output out_9,
  output out_10,
  output out_11
);

  wire _0, _1, _2, _3, _4, _5, _6, _7, _8, _9, _10, _11, _12, _13, _14, _15;

  Decoder #(.select(4), .enable("false")) decoder_1 (
    .out0(_0), .out1(_1), .out2(_2), .out3(_3), .out4(_4), .out5(_5), .out6(_6), .out7(_7), .out8(_8),
    .out9(_9), .out10(_10), .out11(_11), .out12(_12), .out13(_13), .out14(_14), .out15(_15),
    .sel({D, C, B, A}));
  _7_Segment_Display u_7_segment_display_1 (
    .g(out_10), .f(out_8), .a(out_5), .b(out_7), .e(out_6), .d(out_11), .c(out_9), .dp(1'b0));
  or or_1 (out_5, _0, _2, _3, _5, _6, _15, _7, _8, _9, _10, _14);
  or or_2 (out_7, _0, _1, _2, _3, _4, _7, _8, _9, _10, _13);
  or or_3 (out_9, _13, _0, _1, _3, _4, _5, _6, _7, _8, _9, _10, _11);
  or or_4 (out_11, _0, _2, _3, _5, _6, _14, _8, _9, _11, _12, _13);
  or or_5 (out_6, _0, _2, _15, _6, _8, _10, _11, _12, _13, _14);
  or or_6 (out_8, _0, _4, _5, _6, _8, _9, _10, _11, _14, _15);
  or or_7 (out_10, _14, _2, _3, _4, _5, _6, _13, _8, _9, _10, _11, _12, _15);

  // Other names for the same wires on the sheet: A_t = out_5; B_t = out_7; C_t = out_9; D_t = out_11; E = out_6;
  //   F = out_8; G = out_10

  // Notes on the sheet:
  //   D為LSB，A為MSB
  //   這是小數點
endmodule
